# Fritzing sketch switch (saved by Fritzing 0.9.3b)

parts:
  Componente1 = Arduino Mega 2560 (Rev3)
  S1 = Pushbutton [package=THT]

nets:
  N1: Componente1.GND, S1.leg1
  N2: Componente1.D13_PWM, S1.leg0
